# Fritzing sketch DigitalLinearSupply (saved by Fritzing 0.9.0b)

parts:
  R1 = Resistor [tolerance=±5% resistance=10k package=THT]
  C1 = Ceramic Capacitor [capacitance=100nF package="100 mil [THT, multilayer]"]
  R2 = Resistor [tolerance=±5% resistance=10k package=THT]
  C2 = Ceramic Capacitor [capacitance=100nF package="100 mil [THT, multilayer]"]
  Power_plug1 = Power plug
  Power_plug2 = Power plug
  U1 = LM 358 Dual Op-Amp [package="SO 08 [SMD]"]
  U2 = Voltage Regulator [package=to220-adj]
  Part1 = Arduino Pro Mini v13
  R3 = Resistor [tolerance=±5% resistance=240 package=THT]
  R4 = Resistor [tolerance=±20% resistance=6.8k package=THT]
  R5 = Resistor [tolerance=±5% resistance=10k package=THT]
  M1 = DC Motor
  C3 = Ceramic Capacitor [capacitance=100nF package="100 mil [THT, multilayer]"]
  C4 = Electrolytic Capacitor [capacitance=1µF package="100 mil [THT, electrolytic]"]

nets:
  N1: R1.Pin_0, Part1.D10_PWM/SS
  N2: R1.Pin_1, C1.0, R2.Pin_0
  GND: C1.1, C2.1, Power_plug1.GND, Power_plug2.GND, U1.connector3, Part1.GND, R5.Pin_0, M1.pin_2, C3.1, C4.+
  N3: R2.Pin_1, C2.0, U1.connector2
  N4: Power_plug1.VCC, U1.connector7, U2.IN, C3.0
  VCC: Power_plug2.VCC, Part1.VCC
  N5: U1.connector0, U2.ADJ, R3.Pin_0, R4.Pin_1
  N6: U1.connector1, R4.Pin_0, R5.Pin_1
  N7: U2.OUT, R3.Pin_1, M1.pin_1, C4.-

notes:
  Low pass filter to turn PWM into analog voltage
  5V Power Supply
  12V Power Supply
  Square Wave/PWM
  from Arduino
  Op Amp to convert 5V to ~8.75V (more like 8.4V)
  Gain = 1 + (F/G)
  (1 + 6.8/10) = 1.68
  F
  G
  LM317 Receives 0-8.75V and then outputs that + 1.25V to motor to give about 1.25-10V control of motor.
  We'll actually send power into h-bridge to be able to control
  direction of motor.
